# Fritzing sketch voltage_fsr (saved by Fritzing 0.9.2b)
breadboards: 1

parts:
  Part1 = Arduino Uno (Rev3)
  J1 = Basic Force Sensing Resistor (FSR) [package=THT]
  R1 = Resistor [tolerance=±5% resistance=220 package=THT]

nets:
  N1: Part1.A0, J1.pin_1, R1.Pin_0
  N2: Part1.5V, J1.pin_0
  N3: Part1.GND, R1.Pin_1

notes:
  10 k Ohms
