# Fritzing sketch voltage_infrared (saved by Fritzing 0.9.2b)

parts:
  Part1 = Arduino Uno (Rev3)
  J1 = Infrared Proximity Sensor

nets:
  N1: Part1.A0, J1.Vout
  5V: Part1.5V, J1.Vcc
  GND: Part1.GND, J1.GND
