# Fritzing sketch pwm (saved by Fritzing 0.9.2b)
breadboards: 1

parts:
  Part1 = Arduino Uno (Rev3)
  LED1 = LEDs [package=led10mm]
  R1 = Resistor [tolerance=±5% resistance=220 package=THT]

nets:
  N1: Part1.D9_PWM, LED1.A
  N2: Part1.GND, R1.Pin_1
  N3: LED1.C, R1.Pin_0

notes:
  330 ohms
