# Fritzing sketch spealer (saved by Fritzing 0.9.2b)
breadboards: 1

parts:
  Part1 = Arduino Uno (Rev3)
  J1 = Infrared Proximity Sensor
  LED1 = LEDs [package=led10mm]
  R1 = Resistor [tolerance=±5% resistance=220 package=THT]

nets:
  N1: Part1.A0, J1.Vout
  N2: Part1.D9_PWM, LED1.C
  GND: Part1.GND, J1.GND, R1.Pin_0
  5V: Part1.5V, J1.Vcc
  N3: LED1.A, R1.Pin_1
