# Fritzing sketch theremin (saved by Fritzing 0.9.2b)
breadboards: 1

parts:
  Part1 = Arduino Uno (Rev3)
  R1 = Resistor [tolerance=±5% resistance=220 package=THT]
  R2 = Photocell (LDR) [package=THT]
  SPKR1 = Loudspeaker
  J1 = Infrared Proximity Sensor

nets:
  N1: Part1.A0, J1.Vout
  N2: Part1.A1, R1.Pin_1, R2.pin_0
  N3: Part1.D8, SPKR1.pin2
  GND: Part1.GND, R1.Pin_0, SPKR1.pin1, J1.GND
  5V: Part1.5V, R2.pin_1, J1.Vcc

notes:
  10k Ohm
